# Fritzing sketch Tetris Handheld (saved by Fritzing 0.9.3b)

parts:
  WeMos_D1_Mini1 = WeMos D1 Mini
  Buzzer = Piezo Speaker
  part = Resistor [tolerance=±5% resistance=10k package="2010 [SMD]"]
  part_2 = Resistor [tolerance=±5% resistance=2.2k package="2010 [SMD]"]
  part_3 = Resistor [tolerance=±5% resistance=4.7k package="2010 [SMD]"]
  part_4 = Resistor [tolerance=±5% resistance=10k package="2010 [SMD]"]
  part_5 = Resistor [tolerance=±5% resistance=1k package="2010 [SMD]"]
  S1 = Momentary Switch [package=ksa_sealed_tac_switch]
  S2 = Momentary Switch [package=ksa_sealed_tac_switch]
  S3 = Momentary Switch [package=ksa_sealed_tac_switch]
  S4 = Momentary Switch [package=ksa_sealed_tac_switch]
  B_button = Momentary Switch [package=ksa_sealed_tac_switch]
  A_button = Momentary Switch [package=ksa_sealed_tac_switch]
  part_6 = Resistor [tolerance=±5% resistance=4.7k package="2010 [SMD]"]
  R2 = Resistor [tolerance=±5% resistance=4.7k package="2010 [SMD]"]
  U2 = 2.4" TFT LCD screen, SPI, Touch-enabled
  WeMos_D1_Mini_Battery_Shield1 = WeMos D1 Mini Battery Shield
  Main_Switch = Toggle Switch [package=THT]
  Sound_Mute/Unmute = Toggle Switch [package=THT]

nets:
  N1: WeMos_D1_Mini1.A0, part_5.Pin_1
  N2: WeMos_D1_Mini1.D1, B_button.2, R2.Pin_0
  N3: WeMos_D1_Mini1.D2, U2.CS
  N4: WeMos_D1_Mini1.D3, U2.DC
  N5: WeMos_D1_Mini1.D4, U2.RESET
  N6: WeMos_D1_Mini1.D5, U2.SCLK
  N7: WeMos_D1_Mini1.D6, U2.MISO
  N8: WeMos_D1_Mini1.D7, U2.MOSI
  N9: WeMos_D1_Mini1.D8, Sound_Mute/Unmute.COM
  N10: WeMos_D1_Mini1.G, part.Pin_1
  N11: Buzzer.pin2, Sound_Mute/Unmute.L2
  N12: part_2.Pin_0, S3.2
  N13: part_3.Pin_0, S2.2
  N14: part_4.Pin_0, S1.2
  N15: part_5.Pin_0, S4.2
  N16: A_button.2, part_6.Pin_0
  N17: WeMos_D1_Mini_Battery_Shield1.5V, Main_Switch.COM

custom parts:
  2.4" TFT LCD screen, SPI, Touch-enabled: 2.4", ILI9341-based TFT LCD screen with touch-sensing using the XPT2046 controller, SPI-compatible. There is also an SD-card version that is non-touch enabled but uses exactly the same board and pinout. This part is for both, though it should be noted that the SD reader and the touch screen are mutually incompatible
